// Logisim project lab1.circ as structural Verilog: 5 circuits, main circuit main
module main (
  input  [1:0] in_1,
  input  [7:0] in_2,
  output [7:0] out_3
);

  wire [7:0] complement_1_out_2, inverse_1_out_2, origin_1_out_2, shift_1_out_2;

  origin origin_1 (.in_1(in_2), .out_2(origin_1_out_2));
  inverse inverse_1 (.in_1(in_2), .out_2(inverse_1_out_2));
  complement complement_1 (.in_1(in_2), .out_2(complement_1_out_2));
  shift shift_1 (.in_1(in_2), .out_2(shift_1_out_2));
  // Probe on origin_1_out_2
  // Probe on inverse_1_out_2
  // Probe on complement_1_out_2
  // Probe on shift_1_out_2
  Multiplexer #(.enable("false"), .select(2), .width(8)) multiplexer_1 (
    .in0(origin_1_out_2), .in1(inverse_1_out_2), .in2(complement_1_out_2), .in3(shift_1_out_2), .out(out_3),
    .sel(in_1));
endmodule

module origin (
  input  [7:0] in_1,
  output [7:0] out_2
);


  assign out_2 = in_1;
endmodule

module inverse (
  input  [7:0] in_1,
  output [7:0] out_2
);

  wire [6:0] not_1_out;

  not not_1 (not_1_out[0], in_1[0]);
  not not_2 (not_1_out[1], in_1[1]);
  not not_3 (not_1_out[2], in_1[2]);
  not not_4 (not_1_out[3], in_1[3]);
  not not_5 (not_1_out[4], in_1[4]);
  not not_6 (not_1_out[5], in_1[5]);
  not not_7 (not_1_out[6], in_1[6]);
  // Probe on {in_1[7], not_1_out}
  // Probe on in_1
  Multiplexer #(.enable("false"), .width(8)) multiplexer_1 (
    .in0(in_1), .in1({in_1[7], not_1_out}), .out(out_2), .sel(in_1[7]));
  // Probe on out_2
endmodule

module complement (
  input  [7:0] in_1,
  output [7:0] out_2
);

  wire [6:0] not_1_out;
  wire [7:0] adder_1_out;

  not not_1 (not_1_out[0], in_1[0]);
  not not_2 (not_1_out[1], in_1[1]);
  not not_3 (not_1_out[2], in_1[2]);
  not not_4 (not_1_out[3], in_1[3]);
  not not_5 (not_1_out[4], in_1[4]);
  not not_6 (not_1_out[5], in_1[5]);
  not not_7 (not_1_out[6], in_1[6]);
  Adder adder_1 (.a(8'h1), .b({in_1[7], not_1_out}), .out(adder_1_out));  // open: cin, cout
  // Probe on adder_1_out
  // Probe on in_1
  // Probe on out_2
  Multiplexer #(.enable("false"), .width(8)) multiplexer_1 (.in0(in_1), .in1(adder_1_out), .out(out_2), .sel(in_1[7]));
endmodule

module shift (
  input  [7:0] in_1,
  output [7:0] out_2
);

  wire [7:0] adder_1_out, not_2_out;

  not not_1 (not_2_out[7], in_1[7]);
  not not_2 (not_2_out[0], in_1[0]);
  not not_3 (not_2_out[1], in_1[1]);
  not not_4 (not_2_out[2], in_1[2]);
  not not_5 (not_2_out[3], in_1[3]);
  not not_6 (not_2_out[4], in_1[4]);
  not not_7 (not_2_out[5], in_1[5]);
  not not_8 (not_2_out[6], in_1[6]);
  Adder adder_1 (.a(8'h1), .b(not_2_out), .out(adder_1_out));  // open: cin, cout
  // Probe on adder_1_out
  // Probe on {not_2_out[7], in_1[6:0]}
  // Probe on out_2
  Multiplexer #(.enable("false"), .width(8)) multiplexer_1 (
    .in0({not_2_out[7], in_1[6:0]}), .in1(adder_1_out), .out(out_2), .sel(in_1[7]));
endmodule
